# Fritzing sketch Wiring-Drawing-Scheming (saved by Fritzing 0.9.3b)
breadboards: 1

parts:
  KY-1 = Keyes Relay [package=THT]
  Part2 = Lilypad Battery Connect
  F1 = Fan - Ventilador [package=THT]
  Part3 = Arduino Uno (Rev3)
  DHT1 = DHT22 Humidity and Temperature Sensor

nets:
  N1: KY-1.signal, Part3.D2
  5V: KY-1.power, Part3.5V, DHT1.VDD
  GND: KY-1.ground, Part3.GND, DHT1.GND
  N2: KY-1.C, F1.5V
  N3: KY-1.NO, Part2.+
  N4: Part2.-, F1.GND
  N5: Part3.D12/MISO, DHT1.DATA

notes:
  240V AC power supply
  Hijau : Data
  Merah : VCC
  Hitam : Ground
  220 V Fan

custom parts:
  Keyes Relay: The Keyes 5V relay module is suitable for SCM development, home appliance control. It uses a 5V~12V TIL control signal which can control DC / AC signal.
  Fan - Ventilador: Ventilador de 2 pines, se encuentra comunmente en computadoras de escritorio
